// Logisim project 16bit_cpu.circ as structural Verilog: 30 circuits, main circuit main
module main (
);

  wire ac_alu_bases_1_clear, ac_alu_bases_1_inc, ac_alu_bases_1_load, ar_bases_1_clear, ar_bases_1_inc,
       ar_bases_1_load, bus_bases_1_s0, bus_bases_1_s1, bus_bases_1_s2, CLK, cout, dr_bases_1_incr,
       dr_bases_1_load, E_in, FGI, FGO, IEN, iiii, ir_3part_1_i, ir_bases_1_load, memory_bases_1_ld,
       memory_bases_1_stl, pc_bases_1_clear, pc_bases_1_inc, pc_bases_1_load, R, s_1_out, tr_bases_1_load;
  wire [7:0] ac_alu_bases_1_cg, D_i, in_key, out_key;
  wire [11:0] adrs, ar_1_out_6;
  wire [15:0] AC, alu_1_out_7, bus_1_out_11, dr_1_out_6, IRR, pc_1_out_6, ram_1_data, T_i, tr_1_out_6;
  wire [15:12] ar_1_out_6_2;

  R r_1 (.T_i(T_i), .IEN(IEN), .FGI(FGI), .FGO(FGO), .\output (R), .CLK(CLK));
  E e_1 (.D_i(D_i), .cout(cout), .I(iiii), .CLK(CLK), .T_i(T_i), .IR_B(adrs), .AC(AC), .out_8(E_in));
  ALU alu_1 (
    .INPR(in_key), .control_gate(ac_alu_bases_1_cg), .Clock(CLK), .DR(dr_1_out_6), .AC(AC),
    .out_7(alu_1_out_7), .cout(cout), .E(E_in));
  INPR inpr_1 (.in_1({8{1'b0}}), .out(in_key), .load(1'b0), .CLK(CLK));
  // Probe on out_key
  OUTR outr_1 (.OUTPUT(out_key), .T_i(T_i), .I(iiii), .CLK(CLK), .D_i(D_i), .IR_B(adrs), .in_1(bus_1_out_11));
  IR_bases ir_bases_1 (.R(R), .T_i(T_i), .load(ir_bases_1_load));
  TR_bases tr_bases_1 (.R(R), .T_i(T_i), .load(tr_bases_1_load));
  IEN ien_1 (.D_i(D_i), .I(iiii), .T_i(T_i), .R(R), .IR_B(adrs), .CLK(CLK), .\output (IEN));
  I i_1 (.Input(ir_3part_1_i), .out(iiii), .CLK(CLK), .R(R), .T_i(T_i));
  iR__3part ir_3part_1 (.IR(IRR), .address(adrs), .i(ir_3part_1_i), .D_i(D_i));
  PC_bases pc_bases_1 (
    .R(R), .I(iiii), .T_i(T_i), .D_i(D_i), .FGI(FGI), .IR_B_i(adrs), .AC(AC), .CLEAR(pc_bases_1_clear),
    .INC(pc_bases_1_inc), .FGO(FGO), .E(E_in), .load(pc_bases_1_load), .DR(dr_1_out_6));
  DR dr_1 (
    .\input (bus_1_out_11), .out_6(dr_1_out_6), .load(dr_bases_1_load), .INCR(dr_bases_1_incr), .CLK(CLK),
    .CLR(1'b0));
  DR_bases dr_bases_1 (.D_i(D_i), .T_i(T_i), .load(dr_bases_1_load), .INCR(dr_bases_1_incr));
  AC ac_1 (
    .\input (alu_1_out_7), .out_6(AC), .load(ac_alu_bases_1_load), .INCR(ac_alu_bases_1_inc), .CLK(CLK),
    .CLR(ac_alu_bases_1_clear));
  AC_ALU_bases ac_alu_bases_1 (
    .D_i(D_i), .I(iiii), .T_i(T_i), .IR_B_i(adrs), .CG(ac_alu_bases_1_cg), .INC(ac_alu_bases_1_inc),
    .clear(ac_alu_bases_1_clear), .load(ac_alu_bases_1_load));
  IR ir_1 (.\input (bus_1_out_11), .out_4(IRR), .load(ir_bases_1_load), .CLK(CLK));
  TR tr_1 (.\input (bus_1_out_11), .out_6(tr_1_out_6), .load(tr_bases_1_load), .INCR(1'b0), .CLK(CLK), .CLR(1'b0));
  memory_bases memory_bases_1 (.R(R), .I(iiii), .T_i(T_i), .D_i(D_i), .LD(memory_bases_1_ld), .STL(memory_bases_1_stl));
  AR ar_1 (
    .\input (bus_1_out_11), .out_6({ar_1_out_6_2, ar_1_out_6}), .load(ar_bases_1_load),
    .INCR(ar_bases_1_inc), .CLK(CLK), .CLR(ar_bases_1_clear));
  AR_bases ar_bases_1 (
    .I(iiii), .D_i(D_i), .R(R), .T_i(T_i), .load(ar_bases_1_load), .INC(ar_bases_1_inc),
    .clear(ar_bases_1_clear));
  PC pc_1 (
    .\input (bus_1_out_11), .out_6(pc_1_out_6), .load(pc_bases_1_load), .INCR(pc_bases_1_inc), .CLK(CLK),
    .CLR(pc_bases_1_clear));
  FGI fgi_1 (.D_i(D_i), .I(iiii), .T_i(T_i), .CLK(CLK), .IR_B(adrs), .\output (FGI), .INPUT(in_key));
  RAM #(.addrWidth(12), .dataWidth(16), .bus("separate")) ram_1 (
    .addr(ar_1_out_6), .din(bus_1_out_11), .data(ram_1_data), .str(memory_bases_1_stl), .clk(CLK),
    .ld(memory_bases_1_ld));  // open: sel, clr
  S s_1 (.D_I(D_i), .I(iiii), .T_i(T_i), .IR_B(adrs), .out(s_1_out), .CLK(CLK));
  // Probe on ram_1_data
  // Probe on {ar_1_out_6_2, ar_1_out_6}
  // Probe on pc_1_out_6
  // Probe on dr_1_out_6
  // Probe on AC
  // Probe on IRR
  // Probe on tr_1_out_6
  SC___decoder sc_decoder_1 (.out_7(T_i), .S(s_1_out), .CLK(CLK), .D_i(D_i), .T_i(T_i), .R(R), .I(iiii));
  BUS_bases bus_bases_1 (
    .D_i(D_i), .R(R), .T_i(T_i), .I(iiii), .s0(bus_bases_1_s0), .s1(bus_bases_1_s1), .s2(bus_bases_1_s2),
    .IR_B(adrs));
  BUS bus_1 (
    .memory(ram_1_data), .AR({ar_1_out_6_2, ar_1_out_6}), .pc(pc_1_out_6), .DR(dr_1_out_6), .AC(AC),
    .IR(IRR), .TR(tr_1_out_6), .s2(bus_bases_1_s2), .s1(bus_bases_1_s1), .s0(bus_bases_1_s0),
    .out_11(bus_1_out_11));
  FGO fgo_1 (.D_i(D_i), .I(iiii), .T_i(T_i), .CLK(CLK), .IR_B(adrs), .\output (FGO), .output_keyboard(out_key));
  // Probe on bus_1_out_11
  Hex_Digit_Display hex_digit_display_1 (.value(out_key[3:0]));  // open: dp
  Hex_Digit_Display hex_digit_display_2 (.value(out_key[7:4]));  // open: dp
  Clock clock_1 (.out(CLK));
  Hex_Digit_Display hex_digit_display_3 (.value({3'b000, E_in}));  // open: dp

  // Notes on the sheet:
  //   OUTPUT
  //   E
endmodule

module Full_Ader (
  input  cin,
  input  a,
  input  b,
  output sum,
  output cout
);

  wire and_1_out, and_2_out, xor_1_out;

  and and_1 (and_1_out, b, a);
  xor xor_1 (xor_1_out, a, b);
  and and_2 (and_2_out, cin, xor_1_out);
  or or_1 (cout, and_1_out, and_2_out);
  xor xor_2 (sum, cin, xor_1_out);
endmodule

module ALU_1unit (
  input  DR_i,
  input  ac_i__in,
  input  AND,
  input  C_i,
  input  ADD,
  input  DR,
  input  INPR_flag,
  input  INPR_i,
  input  COM,
  input  SHR,
  input  AC_i_1,
  input  SHL,
  input  AC_i_1_2,
  output C_i_1,
  output AC_i
);

  wire and_1_out, and_2_out, and_3_out, and_4_out, and_5_out, and_6_out, and_7_out, full_ader_1_sum,
       not_1_out;

  Full_Ader full_ader_1 (.a(ac_i__in), .b(DR_i), .sum(full_ader_1_sum), .cin(C_i), .cout(C_i_1));
  not not_1 (not_1_out, ac_i__in);
  and and_1 (and_1_out, AND, ac_i__in, DR_i);
  and and_2 (and_2_out, ADD, full_ader_1_sum);
  and and_3 (and_3_out, DR, DR_i);
  and and_4 (and_4_out, INPR_flag, INPR_i);
  and and_5 (and_5_out, COM, not_1_out);
  and and_6 (and_6_out, SHR, AC_i_1);
  and and_7 (and_7_out, SHL, AC_i_1_2);
  or or_1 (AC_i, and_1_out, and_2_out, and_3_out, and_4_out, and_5_out, and_6_out, and_7_out);
endmodule

module ALU (
  input  [7:0] INPR,
  input  [7:0] control_gate,
  input  Clock,
  input  E,
  input  [15:0] DR,
  input  [15:0] AC,
  output [15:0] out_7,
  output cout
);

  wire C1, C2, C3, C4, C5, C6, C7, C8, C9, C10, C11, C12, C13, C14, C15;

  ALU_1unit alu_1unit_1 (
    .AND(control_gate[1]), .ADD(control_gate[2]), .DR(control_gate[3]), .INPR_flag(control_gate[4]),
    .INPR_i(INPR[0]), .COM(control_gate[5]), .SHR(control_gate[6]), .AC_i_1(AC[1]), .SHL(control_gate[7]),
    .AC_i_1_2(E), .AC_i(out_7[0]), .DR_i(DR[0]), .C_i(1'b0), .C_i_1(C1), .ac_i__in(AC[0]));
  ALU_1unit alu_1unit_2 (
    .AND(control_gate[1]), .ADD(control_gate[2]), .DR(control_gate[3]), .INPR_flag(control_gate[4]),
    .INPR_i(INPR[1]), .COM(control_gate[5]), .SHR(control_gate[6]), .AC_i_1(AC[2]), .SHL(control_gate[7]),
    .AC_i_1_2(AC[0]), .AC_i(out_7[1]), .DR_i(DR[1]), .C_i(C1), .C_i_1(C2), .ac_i__in(AC[1]));
  ALU_1unit alu_1unit_3 (
    .AND(control_gate[1]), .ADD(control_gate[2]), .DR(control_gate[3]), .INPR_flag(control_gate[4]),
    .INPR_i(INPR[2]), .COM(control_gate[5]), .SHR(control_gate[6]), .AC_i_1(AC[3]), .SHL(control_gate[7]),
    .AC_i_1_2(AC[1]), .AC_i(out_7[2]), .DR_i(DR[2]), .C_i(C2), .C_i_1(C3), .ac_i__in(AC[2]));
  ALU_1unit alu_1unit_4 (
    .AND(control_gate[1]), .ADD(control_gate[2]), .DR(control_gate[3]), .INPR_flag(control_gate[4]),
    .INPR_i(INPR[3]), .COM(control_gate[5]), .SHR(control_gate[6]), .AC_i_1(AC[4]), .SHL(control_gate[7]),
    .AC_i_1_2(AC[2]), .AC_i(out_7[3]), .DR_i(DR[3]), .C_i(C3), .C_i_1(C4), .ac_i__in(AC[3]));
  ALU_1unit alu_1unit_5 (
    .AND(control_gate[1]), .ADD(control_gate[2]), .DR(control_gate[3]), .INPR_flag(control_gate[4]),
    .INPR_i(INPR[4]), .COM(control_gate[5]), .SHR(control_gate[6]), .AC_i_1(AC[5]), .SHL(control_gate[7]),
    .AC_i_1_2(AC[3]), .AC_i(out_7[4]), .DR_i(DR[4]), .C_i(C4), .C_i_1(C5), .ac_i__in(AC[4]));
  ALU_1unit alu_1unit_6 (
    .AND(control_gate[1]), .ADD(control_gate[2]), .DR(control_gate[3]), .INPR_flag(control_gate[4]),
    .INPR_i(INPR[5]), .COM(control_gate[5]), .SHR(control_gate[6]), .AC_i_1(AC[6]), .SHL(control_gate[7]),
    .AC_i_1_2(AC[4]), .AC_i(out_7[5]), .DR_i(DR[5]), .C_i(C5), .C_i_1(C6), .ac_i__in(AC[5]));
  ALU_1unit alu_1unit_7 (
    .AND(control_gate[1]), .ADD(control_gate[2]), .DR(control_gate[3]), .INPR_flag(control_gate[4]),
    .INPR_i(INPR[6]), .COM(control_gate[5]), .SHR(control_gate[6]), .AC_i_1(AC[7]), .SHL(control_gate[7]),
    .AC_i_1_2(AC[5]), .AC_i(out_7[6]), .DR_i(DR[6]), .C_i(C6), .C_i_1(C7), .ac_i__in(AC[6]));
  ALU_1unit alu_1unit_8 (
    .AND(control_gate[1]), .ADD(control_gate[2]), .DR(control_gate[3]), .INPR_flag(control_gate[4]),
    .INPR_i(INPR[7]), .COM(control_gate[5]), .SHR(control_gate[6]), .AC_i_1(AC[8]), .SHL(control_gate[7]),
    .AC_i_1_2(AC[6]), .AC_i(out_7[7]), .DR_i(DR[7]), .C_i(C7), .C_i_1(C8), .ac_i__in(AC[7]));
  ALU_1unit alu_1unit_9 (
    .AND(control_gate[1]), .ADD(control_gate[2]), .DR(control_gate[3]), .INPR_flag(control_gate[4]),
    .INPR_i(1'b0), .COM(control_gate[5]), .SHR(control_gate[6]), .AC_i_1(AC[9]), .SHL(control_gate[7]),
    .AC_i_1_2(AC[7]), .AC_i(out_7[8]), .DR_i(DR[8]), .C_i(C8), .C_i_1(C9), .ac_i__in(AC[8]));
  ALU_1unit alu_1unit_10 (
    .AND(control_gate[1]), .ADD(control_gate[2]), .DR(control_gate[3]), .INPR_flag(control_gate[4]),
    .INPR_i(1'b0), .COM(control_gate[5]), .SHR(control_gate[6]), .AC_i_1(AC[10]), .SHL(control_gate[7]),
    .AC_i_1_2(AC[8]), .AC_i(out_7[9]), .DR_i(DR[9]), .C_i(C9), .C_i_1(C10), .ac_i__in(AC[9]));
  ALU_1unit alu_1unit_11 (
    .AND(control_gate[1]), .ADD(control_gate[2]), .DR(control_gate[3]), .INPR_flag(control_gate[4]),
    .INPR_i(1'b0), .COM(control_gate[5]), .SHR(control_gate[6]), .AC_i_1(AC[11]), .SHL(control_gate[7]),
    .AC_i_1_2(AC[9]), .AC_i(out_7[10]), .DR_i(DR[10]), .C_i(C10), .C_i_1(C11), .ac_i__in(AC[10]));
  ALU_1unit alu_1unit_12 (
    .AND(control_gate[1]), .ADD(control_gate[2]), .DR(control_gate[3]), .INPR_flag(control_gate[4]),
    .INPR_i(1'b0), .COM(control_gate[5]), .SHR(control_gate[6]), .AC_i_1(AC[12]), .SHL(control_gate[7]),
    .AC_i_1_2(AC[10]), .AC_i(out_7[11]), .DR_i(DR[11]), .C_i(C11), .C_i_1(C12), .ac_i__in(AC[11]));
  ALU_1unit alu_1unit_13 (
    .AND(control_gate[1]), .ADD(control_gate[2]), .DR(control_gate[3]), .INPR_flag(control_gate[4]),
    .INPR_i(1'b0), .COM(control_gate[5]), .SHR(control_gate[6]), .AC_i_1(AC[13]), .SHL(control_gate[7]),
    .AC_i_1_2(AC[11]), .AC_i(out_7[12]), .DR_i(DR[12]), .C_i(C12), .C_i_1(C13), .ac_i__in(AC[12]));
  ALU_1unit alu_1unit_14 (
    .AND(control_gate[1]), .ADD(control_gate[2]), .DR(control_gate[3]), .INPR_flag(control_gate[4]),
    .INPR_i(1'b0), .COM(control_gate[5]), .SHR(control_gate[6]), .AC_i_1(AC[14]), .SHL(control_gate[7]),
    .AC_i_1_2(AC[12]), .AC_i(out_7[13]), .DR_i(DR[13]), .C_i(C13), .C_i_1(C14), .ac_i__in(AC[13]));
  ALU_1unit alu_1unit_15 (
    .AND(control_gate[1]), .ADD(control_gate[2]), .DR(control_gate[3]), .INPR_flag(control_gate[4]),
    .INPR_i(1'b0), .COM(control_gate[5]), .SHR(control_gate[6]), .AC_i_1(AC[15]), .SHL(control_gate[7]),
    .AC_i_1_2(AC[13]), .AC_i(out_7[14]), .DR_i(DR[14]), .C_i(C14), .C_i_1(C15), .ac_i__in(AC[14]));
  ALU_1unit alu_1unit_16 (
    .AND(control_gate[1]), .ADD(control_gate[2]), .DR(control_gate[3]), .INPR_flag(control_gate[4]),
    .INPR_i(1'b0), .COM(control_gate[5]), .SHR(control_gate[6]), .AC_i_1(E), .SHL(control_gate[7]),
    .AC_i_1_2(AC[14]), .AC_i(out_7[15]), .DR_i(DR[15]), .C_i(C15), .C_i_1(cout), .ac_i__in(AC[15]));

  // Other names for the same wires on the sheet: CG[7:0] = control_gate; CLK = Clock; DR_8 = DR[7]; DR_9 = DR[8];
  //   Ein = E; i0 = INPR[0]; i1 = INPR[1]; i2 = INPR[2]; i3 = INPR[3]; i4 = INPR[4]; i5 = INPR[5]; i6 = INPR[6];
  //   i7 = INPR[7]
endmodule

module BUS (
  input  [15:0] memory,
  input  [15:0] AR,
  input  [15:0] pc,
  input  [15:0] DR,
  input  s0,
  input  s1,
  input  s2,
  input  [15:0] AC,
  input  [15:0] IR,
  input  [15:0] TR,
  output [15:0] out_11
);

  wire decoder_1_out1, decoder_1_out2, decoder_1_out3, decoder_1_out4, decoder_1_out5, decoder_1_out6,
       decoder_1_out7;

  Decoder #(.select(3)) decoder_1 (
    .out1(decoder_1_out1), .out2(decoder_1_out2), .out3(decoder_1_out3), .out4(decoder_1_out4),
    .out5(decoder_1_out5), .out6(decoder_1_out6), .out7(decoder_1_out7), .sel({s2, s1, s0}), .en(1'b1));  // open: out0
  assign out_11 = decoder_1_out7 ? memory : 16'bz;  // Controlled_Buffer controlled_buffer_1
  assign out_11 = decoder_1_out1 ? AR : 16'bz;  // Controlled_Buffer controlled_buffer_2
  assign out_11 = decoder_1_out2 ? pc : 16'bz;  // Controlled_Buffer controlled_buffer_3
  assign out_11 = decoder_1_out3 ? DR : 16'bz;  // Controlled_Buffer controlled_buffer_4
  assign out_11 = decoder_1_out4 ? AC : 16'bz;  // Controlled_Buffer controlled_buffer_5
  assign out_11 = decoder_1_out5 ? IR : 16'bz;  // Controlled_Buffer controlled_buffer_6
  assign out_11 = decoder_1_out6 ? TR : 16'bz;  // Controlled_Buffer controlled_buffer_7
endmodule

module IR (
  input  [15:0] \input ,
  input  load,
  input  CLK,
  output [15:0] out_4
);

  Counter #(.width(16), .max('hffff)) counter_1 (
    .load(load), .D(\input ), .count(1'b0), .Q(out_4), .clk(CLK), .clr(1'b0));  // open: carry
endmodule

module AR (
  input  [15:0] \input ,
  input  load,
  input  INCR,
  input  CLK,
  input  CLR,
  output [15:0] out_6
);

  Counter #(.width(12), .max('hfff)) counter_1 (
    .load(load), .D(\input [11:0]), .count(INCR), .Q(out_6[11:0]), .clk(CLK), .clr(CLR));  // open: carry

  assign out_6[15:12] = 4'b0000;
endmodule

module TR (
  input  [15:0] \input ,
  input  load,
  input  INCR,
  input  CLK,
  input  CLR,
  output [15:0] out_6
);

  Counter #(.width(16), .max('hffff)) counter_1 (
    .load(load), .D(\input ), .count(INCR), .Q(out_6), .clk(CLK), .clr(CLR));  // open: carry
endmodule

module PC (
  input  [15:0] \input ,
  input  load,
  input  INCR,
  input  CLK,
  input  CLR,
  output [15:0] out_6
);

  Counter #(.width(12), .max('hfff)) counter_1 (
    .load(load), .D(\input [11:0]), .count(INCR), .Q(out_6[11:0]), .clk(CLK), .clr(CLR));  // open: carry

  assign out_6[15:12] = 4'b0000;
endmodule

module DR (
  input  [15:0] \input ,
  input  load,
  input  INCR,
  input  CLK,
  input  CLR,
  output [15:0] out_6
);

  Counter #(.width(16), .max('hffff)) counter_1 (
    .load(load), .D(\input ), .count(INCR), .Q(out_6), .clk(CLK), .clr(CLR));  // open: carry
endmodule

module AC (
  input  [15:0] \input ,
  input  load,
  input  INCR,
  input  CLK,
  input  CLR,
  output [15:0] out_6
);

  Counter #(.width(16), .max('hffff)) counter_1 (
    .load(load), .D(\input ), .count(INCR), .Q(out_6), .clk(CLK), .clr(CLR));  // open: carry
endmodule

module INPR (
  input  [7:0] in_1,
  input  load,
  input  CLK,
  output [7:0] out
);

  Counter counter_1 (.load(load), .D(in_1), .count(1'b0), .Q(out), .clk(CLK), .clr(1'b0));  // open: carry
endmodule

module OUTR (
  input  [15:0] in_1,
  input  CLK,
  input  [11:0] IR_B,
  input  [15:0] T_i,
  input  [7:0] D_i,
  input  I,
  output [7:0] OUTPUT
);

  wire and_1_out, and_2_out;

  Counter counter_1 (.load(and_1_out), .D(in_1[7:0]), .count(1'b0), .Q(OUTPUT), .clk(CLK), .clr(1'b0));  // open: carry
  and and_1 (and_1_out, IR_B[10], and_2_out);
  and and_2 (and_2_out, T_i[3], I, D_i[7]);
endmodule

module AR_bases (
  input  I,
  input  [7:0] D_i,
  input  R,
  input  [15:0] T_i,
  output load,
  output INC,
  output clear
);

  wire and_1_out, and_2_out, and_3_out, not_1_out, not_2_out;

  not not_1 (not_1_out, R);
  not not_2 (not_2_out, D_i[7]);
  and and_1 (and_1_out, I, not_2_out, T_i[3]);
  and and_2 (and_2_out, T_i[2], not_1_out);
  and and_3 (and_3_out, not_1_out, T_i[0]);
  and and_4 (INC, D_i[5], T_i[4]);
  and and_5 (clear, T_i[0], R);
  or or_1 (load, and_1_out, and_2_out, and_3_out);
endmodule

module E (
  input  [7:0] D_i,
  input  cout,
  input  I,
  input  CLK,
  input  [15:0] T_i,
  input  [11:0] IR_B,
  input  [15:0] AC,
  output out_8
);

  wire and_1_out, and_2_out, and_3_out, and_4_out, and_5_out, and_6_out, and_7_out, and_8_out, and_9_out,
       and_10_out, not_1_out, not_2_out, not_3_out, not_4_out, or_1_out, or_2_out;

  not not_1 (not_1_out, I);
  and and_1 (and_1_out, D_i[7], not_1_out, T_i[3]);
  not not_2 (not_2_out, cout);
  not not_3 (not_3_out, AC[15]);
  and and_2 (and_2_out, D_i[1], not_2_out, T_i[5]);
  and and_3 (and_3_out, and_1_out, IR_B[10]);
  and and_4 (and_4_out, and_1_out, IR_B[8]);
  and and_5 (and_5_out, and_1_out, IR_B[7], not_4_out);
  not not_4 (not_4_out, AC[0]);
  and and_6 (and_6_out, and_1_out, IR_B[6], not_3_out);
  and and_7 (and_7_out, and_1_out, IR_B[8]);
  and and_8 (and_8_out, D_i[1], cout, T_i[5]);
  and and_9 (and_9_out, and_1_out, AC[0], IR_B[7]);
  and and_10 (and_10_out, and_1_out, IR_B[6], AC[15]);
  or or_1 (or_1_out, and_7_out, and_8_out, and_9_out, and_10_out);
  or or_2 (or_2_out, and_2_out, and_3_out, and_4_out, and_5_out, and_6_out);
  J_K_Flip_Flop j_k_ff_1 (.J(or_1_out), .clk(CLK), .K(or_2_out), .Q(out_8));  // open: Qn, preset, en, reset

  // Other names for the same wires on the sheet: AC_0 = AC[0]; AC_15 = AC[15]
endmodule

module SC___decoder (
  input  CLK,
  input  S,
  input  [15:0] T_i,
  input  I,
  input  R,
  input  [7:0] D_i,
  output [15:0] out_7
);

  wire and_1_out, and_2_out, and_3_out, and_4_out, and_5_out, and_6_out, and_7_out, and_8_out, not_1_out,
       not_2_out, or_1_out, or_2_out, or_3_out;
  wire [3:0] counter_1_q;

  not not_1 (not_1_out, I);
  or or_1 (or_1_out, and_2_out, and_1_out, and_3_out, and_6_out, and_7_out, and_8_out);
  and and_1 (and_1_out, T_i[3], not_1_out, D_i[7]);
  and and_2 (and_2_out, I, D_i[7], T_i[3]);
  not not_2 (not_2_out, or_1_out);
  and and_3 (and_3_out, R, T_i[2]);
  and and_4 (and_4_out, or_1_out, S);
  Counter #(.width(4), .max('hf)) counter_1 (
    .load(and_4_out), .D(4'b0000), .count(and_5_out), .Q(counter_1_q), .clk(CLK));  // open: carry, clr
  and and_5 (and_5_out, not_2_out, S);
  and and_6 (and_6_out, T_i[6], D_i[6]);
  and and_7 (and_7_out, T_i[4], or_2_out);
  or or_2 (or_2_out, D_i[4], D_i[3]);
  Decoder #(.select(4)) decoder_1 (
    .out0(out_7[0]), .out1(out_7[1]), .out2(out_7[2]), .out3(out_7[3]), .out4(out_7[4]), .out5(out_7[5]),
    .out6(out_7[6]), .out7(out_7[7]), .out8(out_7[8]), .out9(out_7[9]), .out10(out_7[10]), .out11(out_7[11]),
    .out12(out_7[12]), .out13(out_7[13]), .out14(out_7[14]), .out15(out_7[15]), .sel(counter_1_q));  // open: en
  and and_8 (and_8_out, T_i[5], or_3_out);
  or or_3 (or_3_out, D_i[5], D_i[2], D_i[1], D_i[0]);
endmodule

module iR__3part (
  input  [15:0] IR,
  output [11:0] address,
  output i,
  output [7:0] D_i
);

  Decoder #(.select(3)) decoder_1 (
    .out0(D_i[0]), .out1(D_i[1]), .out2(D_i[2]), .out3(D_i[3]), .out4(D_i[4]), .out5(D_i[5]), .out6(D_i[6]),
    .out7(D_i[7]), .sel(IR[14:12]));  // open: en

  assign address = IR[11:0];
  assign i = IR[15];
endmodule

module I (
  input  [15:0] T_i,
  input  CLK,
  input  R,
  input  Input,
  output out
);

  wire and_1_out, and_2_out, not_1_out, not_2_out;

  not not_1 (not_1_out, R);
  not not_2 (not_2_out, Input);
  and and_1 (and_1_out, T_i[2], not_1_out, Input);
  and and_2 (and_2_out, T_i[2], not_1_out, not_2_out);
  J_K_Flip_Flop j_k_ff_1 (.J(and_1_out), .clk(CLK), .K(and_2_out), .Q(out));  // open: Qn, preset, en, reset
endmodule

module PC_bases (
  input  R,
  input  I,
  input  [15:0] T_i,
  input  [7:0] D_i,
  input  FGI,
  input  FGO,
  input  [15:0] DR,
  input  [11:0] IR_B_i,
  input  E,
  input  [15:0] AC,
  output CLEAR,
  output INC,
  output load
);

  wire and_1_out, and_2_out, and_4_out, and_5_out, and_6_out, and_7_out, and_8_out, and_9_out, and_10_out,
       and_11_out, and_12_out, and_13_out, and_14_out, nor_1_out, nor_2_out, not_1_out, not_2_out, not_3_out,
       not_4_out;

  nor nor_1 (nor_1_out, DR[15], DR[14], DR[13], DR[12], DR[11], DR[10], DR[9], DR[8], DR[7], DR[6], DR[5], DR[4], DR[3], DR[2], DR[1], DR[0]);
  nor nor_2 (nor_2_out, AC[15], AC[14], AC[13], AC[12], AC[11], AC[10], AC[9], AC[8], AC[7], AC[6], AC[5], AC[4], AC[3], AC[2], AC[1], AC[0]);
  not not_1 (not_1_out, I);
  and and_1 (and_1_out, T_i[3], not_1_out, D_i[7]);
  and and_2 (and_2_out, I, T_i[3], D_i[7]);
  not not_2 (not_2_out, R);
  not not_3 (not_3_out, AC[15]);
  not not_4 (not_4_out, E);
  and and_3 (CLEAR, R, T_i[1]);
  and and_4 (and_4_out, not_2_out, T_i[1]);
  and and_5 (and_5_out, R, T_i[2]);
  and and_6 (and_6_out, T_i[6], nor_1_out, D_i[6]);
  and and_7 (and_7_out, and_1_out, IR_B_i[4], not_3_out);
  and and_8 (and_8_out, and_1_out, IR_B_i[3], AC[15]);
  and and_9 (and_9_out, and_1_out, IR_B_i[2], nor_2_out);
  and and_10 (and_10_out, and_1_out, IR_B_i[1], not_4_out);
  and and_11 (and_11_out, and_2_out, IR_B_i[9], FGI);
  and and_12 (and_12_out, FGO, IR_B_i[8], and_2_out);
  and and_13 (and_13_out, D_i[4], T_i[4]);
  and and_14 (and_14_out, T_i[5], D_i[5]);
  or or_1 (INC, and_4_out, and_5_out, and_6_out, and_7_out, and_8_out, and_9_out, and_10_out, and_11_out, and_12_out);
  or or_2 (load, and_13_out, and_14_out);

  // Other names for the same wires on the sheet: T4 = T_i[4]; T5 = T_i[5]
endmodule

module DR_bases (
  input  [7:0] D_i,
  input  [15:0] T_i,
  output load,
  output INCR
);

  wire or_1_out;

  or or_1 (or_1_out, D_i[0], D_i[1], D_i[2], D_i[6]);
  and and_1 (load, or_1_out, T_i[4]);
  and and_2 (INCR, D_i[6], T_i[5]);
endmodule

module memory_bases (
  input  R,
  input  I,
  input  [15:0] T_i,
  input  [7:0] D_i,
  output LD,
  output STL
);

  wire and_1_out, and_2_out, and_3_out, and_4_out, and_5_out, and_6_out, not_1_out, not_2_out, or_1_out,
       or_2_out;

  not not_1 (not_1_out, D_i[7]);
  or or_1 (or_1_out, D_i[3], D_i[5]);
  not not_2 (not_2_out, R);
  or or_2 (or_2_out, D_i[0], D_i[1], D_i[2], D_i[6]);
  and and_1 (and_1_out, R, T_i[1]);
  and and_2 (and_2_out, not_2_out, T_i[1]);
  and and_3 (and_3_out, I, T_i[3], not_1_out);
  and and_4 (and_4_out, T_i[4], or_2_out);
  and and_5 (and_5_out, T_i[6], D_i[6]);
  and and_6 (and_6_out, T_i[4], or_1_out);
  or or_3 (LD, and_2_out, and_3_out, and_4_out);
  or or_4 (STL, and_1_out, and_5_out, and_6_out);
endmodule

module IR_bases (
  input  R,
  input  [15:0] T_i,
  output load
);

  wire not_1_out;

  not not_1 (not_1_out, R);
  and and_1 (load, not_1_out, T_i[1]);
endmodule

module TR_bases (
  input  R,
  input  [15:0] T_i,
  output load
);

  and and_1 (load, R, T_i[0]);
endmodule

module AC_ALU_bases (
  input  [7:0] D_i,
  input  I,
  input  [15:0] T_i,
  input  [11:0] IR_B_i,
  output load,
  output [7:0] CG,
  output INC,
  output clear
);

  wire and_1_out, and_2_out, not_1_out;

  and and_1 (and_1_out, D_i[7], I, T_i[3]);
  not not_1 (not_1_out, I);
  and and_2 (and_2_out, D_i[7], not_1_out, T_i[3]);
  and and_3 (CG[1], D_i[0], T_i[5]);
  and and_4 (CG[2], T_i[5], D_i[1]);
  and and_5 (CG[3], D_i[2], T_i[5]);
  and and_6 (CG[4], and_1_out, IR_B_i[11]);
  and and_7 (CG[5], and_2_out, IR_B_i[9]);
  and and_8 (CG[6], and_2_out, IR_B_i[7]);
  and and_9 (CG[7], and_2_out, IR_B_i[6]);
  and and_10 (INC, and_2_out, IR_B_i[5]);
  and and_11 (clear, and_2_out, IR_B_i[11]);
  or or_1 (CG[0], CG[1], CG[2], CG[3], CG[4], CG[5], CG[6], CG[7]);

  assign load = CG[0];
endmodule

module BUS_bases (
  input  [7:0] D_i,
  input  R,
  input  [15:0] T_i,
  input  I,
  input  [11:0] IR_B,
  output s0,
  output s1,
  output s2
);

  wire and_1_out, and_2_out, and_3_out, and_4_out, and_5_out, and_6_out, and_7_out, and_8_out, and_9_out,
       and_10_out, and_11_out, and_12_out, not_1_out, not_2_out, or_1_out, or_2_out, or_3_out, or_4_out,
       or_5_out;

  and and_1 (and_1_out, D_i[7], I, T_i[3]);
  not not_1 (not_1_out, R);
  or or_1 (or_1_out, D_i[0], D_i[1], D_i[2], D_i[6]);
  and and_2 (and_2_out, D_i[4], T_i[4]);
  and and_3 (and_3_out, D_i[5], T_i[5]);
  and and_4 (and_4_out, D_i[5], T_i[4]);
  and and_5 (and_5_out, D_i[6], T_i[6]);
  and and_6 (and_6_out, D_i[3], T_i[4]);
  and and_7 (and_7_out, and_1_out, IR_B[10]);
  and and_8 (and_8_out, not_1_out, T_i[2]);
  and and_9 (and_9_out, R, T_i[1]);
  and and_10 (and_10_out, not_1_out, T_i[1]);
  not not_2 (not_2_out, D_i[7]);
  and and_11 (and_11_out, not_2_out, I, T_i[3]);
  and and_12 (and_12_out, T_i[4], or_1_out);
  or or_2 (or_2_out, and_2_out, and_3_out);
  or or_3 (or_3_out, T_i[0], and_4_out);
  or or_4 (or_4_out, and_6_out, and_7_out);
  or or_5 (or_5_out, and_10_out, and_11_out, and_12_out);
  Priority_Encoder priority_encoder_1 (
    .in0(1'b1), .in1(or_2_out), .in2(or_3_out), .in3(and_5_out), .in4(or_4_out), .in5(and_8_out),
    .in6(and_9_out), .in7(or_5_out), .out({s2, s1, s0}));  // open: en_in, gs, en_out
endmodule

module S (
  input  [7:0] D_I,
  input  I,
  input  [15:0] T_i,
  input  CLK,
  input  [11:0] IR_B,
  output out
);

  wire and_1_out, and_2_out, not_1_out;

  not not_1 (not_1_out, I);
  and and_1 (and_1_out, D_I[7], not_1_out, T_i[3]);
  and and_2 (and_2_out, and_1_out, IR_B[0]);
  J_K_Flip_Flop j_k_ff_1 (.J(1'b0), .clk(CLK), .K(1'b0), .Qn(out), .preset(and_2_out));  // open: Q, en, reset
endmodule

module R (
  input  [15:0] T_i,
  input  IEN,
  input  FGI,
  input  CLK,
  input  FGO,
  output \output 
);

  wire and_1_out, and_2_out, not_1_out, not_2_out, not_3_out, or_1_out;

  or or_1 (or_1_out, FGI, FGO);
  not not_1 (not_1_out, T_i[1]);
  not not_2 (not_2_out, T_i[2]);
  and and_1 (and_1_out, T_i[2], \output );
  not not_3 (not_3_out, T_i[0]);
  and and_2 (and_2_out, not_3_out, not_1_out, not_2_out, IEN, or_1_out);
  J_K_Flip_Flop j_k_ff_1 (.J(and_2_out), .clk(CLK), .K(and_1_out), .Q(\output ));  // open: Qn, preset, en, reset
endmodule

module IEN (
  input  [7:0] D_i,
  input  I,
  input  CLK,
  input  [15:0] T_i,
  input  R,
  input  [11:0] IR_B,
  output \output 
);

  wire and_1_out, and_2_out, and_3_out, and_4_out, or_1_out;

  and and_1 (and_1_out, D_i[7], I, T_i[3]);
  and and_2 (and_2_out, and_1_out, IR_B[7]);
  and and_3 (and_3_out, T_i[2], R);
  and and_4 (and_4_out, and_1_out, IR_B[6]);
  or or_1 (or_1_out, and_3_out, and_4_out);
  J_K_Flip_Flop j_k_ff_1 (.J(and_2_out), .clk(CLK), .K(or_1_out), .Q(\output ));  // open: Qn, preset, en, reset
endmodule

module FGI (
  input  [7:0] INPUT,
  input  [7:0] D_i,
  input  I,
  input  [15:0] T_i,
  input  CLK,
  input  [11:0] IR_B,
  output \output 
);

  wire and_1_out, and_2_out, or_1_out;

  and and_1 (and_1_out, D_i[7], I, T_i[3]);
  and and_2 (and_2_out, and_1_out, IR_B[11]);
  or or_1 (or_1_out, INPUT[7], INPUT[6], INPUT[5], INPUT[4], INPUT[3], INPUT[2], INPUT[1], INPUT[0]);
  J_K_Flip_Flop j_k_ff_1 (.J(or_1_out), .clk(CLK), .K(and_2_out), .Q(\output ));  // open: Qn, preset, en, reset
endmodule

module FGO (
  input  [7:0] output_keyboard,
  input  [7:0] D_i,
  input  I,
  input  [15:0] T_i,
  input  CLK,
  input  [11:0] IR_B,
  output \output 
);

  wire and_1_out, and_2_out, nor_1_out;

  and and_1 (and_1_out, D_i[7], I, T_i[3]);
  and and_2 (and_2_out, and_1_out, IR_B[10]);
  nor nor_1 (nor_1_out, output_keyboard[7], output_keyboard[6], output_keyboard[5], output_keyboard[4], output_keyboard[3], output_keyboard[2], output_keyboard[1], output_keyboard[0]);
  J_K_Flip_Flop j_k_ff_1 (.J(nor_1_out), .clk(CLK), .K(and_2_out), .Q(\output ));  // open: Qn, preset, en, reset
endmodule
